// Logisim project Architecture.circ as structural Verilog: 1 circuit, main circuit Architecture1
module Architecture1 (
  output out_1,
  output out_2,
  output out_3,
  output out_4,
  output N,
  output Z,
  output C,
  output out_8,
  output out_9,
  output out_10,
  output out_11,
  output out_12,
  output out_13,
  output out_14,
  output out_15,
  output out_16
);

  wire alu_with_controls_1_p13, alu_with_controls_1_p14, alu_with_controls_1_p16, clock_1_out,
       instruction_register_1_p17, instruction_register_1_p18, instruction_register_1_p20, or_1_out,
       program_counter_1_p1, program_counter_1_p5, program_counter_1_p9, program_counter_1_p12,
       program_counter_1_p13, program_counter_1_p14, program_counter_1_p15, pull_resistor_7_node, R1_p1,
       R1_p3, R1_p5, R1_p10, R1_p13, R1_p15, R2_p1, R2_p3, R2_p5, R2_p10, R2_p13, R2_p15, R3_p1, R3_p3,
       R3_p5, R3_p10, R3_p13, R3_p15, R4_p1, R4_p3, R4_p5, R4_p10, R4_p13, R4_p15, ram_rom_with_mar_1_p1,
       ram_rom_with_mar_1_p3, ram_rom_with_mar_1_p4, ram_rom_with_mar_1_p5, ram_rom_with_mar_1_p6;
  wire [1:0] alu_with_controls_1_p17;
  wire [3:0] R1_p12;

  Clock clock_1 (.out(clock_1_out));
  // General_Purpose_Register R1: pin names not known; wires that end beside it: R1_p1, clock_1_out, R1_p3, R1_p12[3], R1_p5, R1_p12[3], R1_p12[2], R1_p12[2], R1_p12[1], R1_p10, R1_p12[1], R1_p12[0], R1_p13, R1_p12[0], R1_p15
  LED led_1 (.in(R1_p5));
  // General_Purpose_Register R3: pin names not known; wires that end beside it: R3_p1, clock_1_out, R3_p3, R1_p12[3], R3_p5, R1_p12[3], R1_p12[2], R1_p12[2], R1_p12[1], R3_p10, R1_p12[1], R1_p12[0], R3_p13, R1_p12[0], R3_p15
  LED led_2 (.in(R3_p5));
  LED led_3 (.in(R1_p15));
  LED led_4 (.in(R1_p13));
  LED led_5 (.in(R1_p10));
  LED led_6 (.in(R3_p10));
  LED led_7 (.in(R3_p15));
  LED led_8 (.in(R3_p13));
  // General_Purpose_Register R2: pin names not known; wires that end beside it: R2_p1, clock_1_out, R2_p3, R1_p12[3], R2_p5, R1_p12[3], R1_p12[2], R1_p12[2], R1_p12[1], R2_p10, R1_p12[1], R1_p12[0], R2_p13, R1_p12[0], R2_p15
  // General_Purpose_Register R4: pin names not known; wires that end beside it: R4_p1, clock_1_out, R4_p3, R1_p12[3], R4_p5, R1_p12[3], R1_p12[2], R1_p12[2], R1_p12[1], R4_p10, R1_p12[1], R1_p12[0], R4_p13, R1_p12[0], R4_p15
  LED led_9 (.in(R2_p13));
  LED led_10 (.in(R2_p10));
  LED led_11 (.in(R2_p5));
  LED led_12 (.in(R4_p10));
  LED led_13 (.in(R4_p5));
  LED led_14 (.in(R4_p13));
  LED led_15 (.in(R2_p15));
  LED led_16 (.in(R4_p15));
  // RAM_ROM_with_MAR ram_rom_with_mar_1: pin names not known; wires that end beside it: ram_rom_with_mar_1_p1, clock_1_out, ram_rom_with_mar_1_p3, ram_rom_with_mar_1_p4, ram_rom_with_mar_1_p5, ram_rom_with_mar_1_p6, R1_p12, R1_p12, R1_p12[0], R1_p12[1], R1_p12[2], R1_p12[3]
  LED led_17 (.in(R1_p12[2]));
  LED led_18 (.in(R1_p12[3]));
  Pull_Resistor pull_resistor_1 (.node(R1_p12[3]));
  Pull_Resistor pull_resistor_2 (.node(R1_p12[2]));
  LED led_19 (.in(R1_p12[1]));
  LED led_20 (.in(R1_p12[0]));
  Pull_Resistor pull_resistor_3 (.node(R1_p12[0]));
  Pull_Resistor pull_resistor_4 (.node(R1_p12[1]));
  // Program_counter program_counter_1: pin names not known; wires that end beside it: program_counter_1_p1, R1_p12[3], R1_p12[3], R1_p12[2], program_counter_1_p5, R1_p12[2], R1_p12[1], R1_p12[1], program_counter_1_p9, R1_p12[0], R1_p12[0], program_counter_1_p12, program_counter_1_p13, program_counter_1_p14, program_counter_1_p15, clock_1_out
  LED led_21 (.in(program_counter_1_p1));
  LED led_22 (.in(program_counter_1_p5));
  LED led_23 (.in(program_counter_1_p9));
  LED led_24 (.in(program_counter_1_p12));
  // ALU_with_controls alu_with_controls_1: pin names not known; wires that end beside it: R1_p12[3], R1_p12[2], R1_p12[1], R1_p12[0], R1_p12[3], R1_p12[2], R1_p12[1], R1_p12[3], R1_p12[0], R1_p12[2], R1_p12[1], R1_p12[0], alu_with_controls_1_p13, alu_with_controls_1_p14, clock_1_out, alu_with_controls_1_p16, alu_with_controls_1_p17, out_1, out_2, out_3, out_4
  // Instruction_Register instruction_register_1: pin names not known; wires that end beside it: R1_p12[3], R1_p12[2], R1_p12[1], R1_p12[0], R1_p12[3], R1_p12[2], R1_p12[1], R1_p12[0], out_9, out_10, out_11, out_12, out_13, out_14, out_15, out_16, instruction_register_1_p17, instruction_register_1_p18, clock_1_out, instruction_register_1_p20
  Control_logic_main main_1 (
    .in_9(clock_1_out), .in_10(out_1), .in_11(N), .in_12(Z), .in_13(C), .in_1(out_9), .in_2(out_10),
    .in_3(out_11), .in_4(out_12), .in_5(out_13), .in_6(out_14), .in_7(out_15), .in_8(out_16),
    .MARin(ram_rom_with_mar_1_p1), .out_34(ram_rom_with_mar_1_p3), .RAMData(ram_rom_with_mar_1_p4),
    .out_36(ram_rom_with_mar_1_p5), .ROM2out(ram_rom_with_mar_1_p6), .R1in(R1_p1), .out_15(R1_p3),
    .R2in(R2_p1), .out_17(R2_p3), .R3in(R3_p1), .R3out(R3_p3), .out_20(R4_p1), .R4out(R4_p3),
    .out_22(program_counter_1_p13), .PCClkEN(program_counter_1_p14), .PCout(program_counter_1_p15),
    .out_25(alu_with_controls_1_p13), .Yin(alu_with_controls_1_p14), .out_27(alu_with_controls_1_p16),
    .MSBin(instruction_register_1_p17), .LSBin(instruction_register_1_p18),
    .out_30(instruction_register_1_p20), .DO1(alu_with_controls_1_p17[1]), .out_32(alu_with_controls_1_p17[0]));
  or or_1 (or_1_out, alu_with_controls_1_p17[0], alu_with_controls_1_p17[1]);
  Pull_Resistor pull_resistor_5 (.node(out_4));
  Pull_Resistor pull_resistor_6 (.node(out_2));
  Pull_Resistor pull_resistor_7 (.node(pull_resistor_7_node));
  // General_Purpose_Register Status_Register: pin names not known; wires that end beside it: or_1_out, clock_1_out, 1'b1, out_4, N, out_3, Z, out_2, C, pull_resistor_7_node, out_8

  // Notes on the sheet:
  //   R1
  //   R3
  //   R2
  //   R4
  //   Status Register
endmodule
